# Fritzing sketch ESP32-Scanner (saved by Fritzing 0.9.8b)
perfboards: 1

parts:
  U1 = ESP32-38PinWide [part_number=ESP32-38PinWide]  # not connected
  J1 = 2.1mm Barrel Jack with Terminal Block
  J2 = female pin header, 19 pins [form="♀ (female)"]
  J3 = female pin header, 19 pins [form="♀ (female)"]  # not connected

nets:
  N1: J1.POS, J2.pin1
  N2: J1.NEG, J2.pin2

custom parts:
  ESP32-38PinWide: Generic 38-Pin ESP32 with wide format (only access to one side of pins on a breadboard) based on Stephen Lilley's HiLetgo ESP-WROOM-32 ESP32 ESP-32S Development Board.
